// Digital circuit LOAD.dig as structural Verilog
module LOAD (
  input  [3:0] Function,
  input  EN,
  input  [15:0] I3_I4,
  input  [15:0] q,
  input  [15:0] RAM_in,
  output [15:0] p,
  output p_CLK,
  output [15:0] RAM_addr
);

  wire delay_1_out;

  Delay #(.delayTime(10)) delay_1 (.in(EN), .out(delay_1_out));
  Multiplexer #(.Selector_Bits(4), .Bits(16)) multiplexer_1 (
    .sel(Function), .in_0({16{1'b0}}), .in_1(I3_I4), .in_2(q), .in_3(RAM_in), .in_4({16{1'b0}}),
    .in_5({16{1'b0}}), .in_6({16{1'b0}}), .in_7({16{1'b0}}), .in_8({16{1'b0}}), .in_9({16{1'b0}}),
    .in_10({16{1'b0}}), .in_11({16{1'b0}}), .in_12({16{1'b0}}), .in_13({16{1'b0}}), .in_14({16{1'b0}}),
    .in_15({16{1'b0}}), .out(p));
  Multiplexer #(.Selector_Bits(4)) multiplexer_2 (
    .sel(Function), .in_0(1'b0), .in_1(delay_1_out), .in_2(delay_1_out), .in_3(delay_1_out),
    .in_4(delay_1_out), .in_5(delay_1_out), .in_6(1'b0), .in_7(1'b0), .in_8(1'b0), .in_9(1'b0), .in_10(1'b0),
    .in_11(1'b0), .in_12(1'b0), .in_13(1'b0), .in_14(1'b0), .in_15(1'b0), .out(p_CLK));

  assign RAM_addr = I3_I4;
endmodule
