// Digital circuit Main.dig as structural Verilog
module Main (
  input  clk,
  output [15:0] out_1,
  output [15:0] out_2
);

  wire button_1_out, control_unit_1_ram_clk;
  wire [15:0] control_unit_1_ram_addr, control_unit_1_ram_out, ramdualport_1_d;
  wire [31:0] d_ff_1_q, rom_1_d;

  ROM #(.AddrBits(16), .Bits(32)) rom_1 (.A(out_2), .sel(1'b1), .D(rom_1_d));
  Button button_1 (.out(button_1_out));
  D_FF #(.Bits(32)) d_ff_1 (.D(rom_1_d), .C(clk), .Q(d_ff_1_q));  // open: nQ
  Control_Unit control_unit_1 (
    .Instruction(d_ff_1_q), .CLK(clk), .RAM_in(ramdualport_1_d), .PROG_reset(button_1_out), .R0(out_1),
    .RAM_out(control_unit_1_ram_out), .RAM_CLK(control_unit_1_ram_clk), .RAM_addr(control_unit_1_ram_addr),
    .PROG_Counter(out_2));
  RAMDualPort #(.AddrBits(16), .Bits(16)) ramdualport_1 (
    .A(control_unit_1_ram_addr), .Din(control_unit_1_ram_out), .str(1'b1), .C(control_unit_1_ram_clk),
    .ld(1'b1), .D(ramdualport_1_d));

  // Notes on the sheet:
  //   clk: Hz: 200
  //   contents of rom_1 (hex, n*v repeats v):
  //   1010001,1020001,24000102,2020100,2010000,50000002
endmodule
